// Logisim project WBramki.circ as structural Verilog: 1 circuit, main circuit main
module main (
  input  A,
  input  B,
  input  C,
  input  D,
  input  A_2,
  input  B_2,
  input  C_2,
  input  D_2
);

  wire n7474_1_p2, n7474_1_p5, n7474_2_p2, n7474_2_p5, nand_1_out, nand_2_out, nand_3_out, nand_4_out,
       nand_5_out, nand_6_out, nand_7_out, not_1_out, not_2_out;

  not not_1 (not_1_out, A);
  not not_2 (not_2_out, A_2);
  nand nand_1 (nand_1_out, not_1_out, B, D);
  nand nand_2 (nand_2_out, A, C);
  nand nand_3 (nand_3_out, not_2_out, B_2, D_2);
  nand nand_4 (nand_4_out, A_2, C_2);
  nand nand_5 (nand_5_out, B_2, C_2, D_2);
  nand nand_6 (nand_6_out, nand_1_out, nand_2_out);
  LED led_1 (.in(nand_6_out));
  LED led_2 (.in(n7474_1_p5));
  nand nand_7 (nand_7_out, nand_3_out, nand_5_out, nand_4_out);
  LED led_3 (.in(n7474_2_p5));
  LED led_4 (.in(nand_7_out));
  // _7474 7474_1: pin names not known; wires that end beside it: 1'b0, n7474_1_p2, nand_6_out, 1'b0, n7474_1_p5, n7474_1_p2, 1'b0, 1'b1
  // _7474 7474_2: pin names not known; wires that end beside it: 1'b0, n7474_2_p2, nand_7_out, 1'b0, n7474_2_p5, n7474_2_p2, 1'b0, 1'b1
endmodule
