// Logisim project WUkłady.circ as structural Verilog: 1 circuit, main circuit main
module main (
  input  a,
  input  a_2,
  input  b,
  input  b_2,
  input  c,
  input  c_2,
  input  d,
  input  d_2
);

  wire n7400_1_p2, n7400_1_p3, n7400_1_p4, n7400_1_p8, n7400_1_p11, n7400_1_p12, n7400_2_p10, n7400_2_p11,
       n7400_2_p18, n7400_2_p19, n7474_1_p3, n7474_1_p5, n7474_1_p6;

  // _7400 7400_1: pin names not known; wires that end beside it: d, n7400_1_p2, n7400_1_p3, n7400_1_p4, n7400_1_p4, c, a, n7400_1_p8, n7400_1_p2, n7400_1_p3, n7400_1_p11, n7400_1_p12, n7400_1_p4, d, c, b, a
  // _7404 7404_1: pin names not known; wires that end beside it: n7400_1_p11, d, n7400_1_p12, b, n7400_1_p3, n7400_1_p11
  // _7410 7410_1: pin names not known; wires that end beside it: n7400_1_p8, d, n7400_1_p12, a, c, b, n7400_1_p2, n7400_1_p3, n7400_1_p11, n7400_1_p12, n7400_1_p4, c, b, a
  // _7474 7474_1: pin names not known; wires that end beside it: 1'b1, 1'b1, n7474_1_p3, 1'b0, n7474_1_p5, n7474_1_p6, 1'b0
  LED led_1 (.in(n7474_1_p3));
  // _7400 7400_2: pin names not known; wires that end beside it: 1'b0, n7474_1_p6, n7474_1_p3, n7474_1_p6, n7474_1_p5, 1'b1, 1'b1, 1'b0, n7474_1_p5, n7400_2_p10, n7400_2_p11, n7400_2_p11, c_2, a_2, 1'b0, n7474_1_p5, n7400_2_p10, n7400_2_p18, n7400_2_p19, n7400_2_p11, d_2, c_2, b_2, a_2
  // _7404 7404_2: pin names not known; wires that end beside it: 1'b1, n7400_2_p18, d_2, n7400_2_p19, b_2, 1'b0, n7400_2_p10, n7400_2_p18
  // _7410 7410_2: pin names not known; wires that end beside it: 1'b0, n7474_1_p6, 1'b1, n7400_2_p19, a_2, 1'b0, n7400_2_p10, n7400_2_p18, n7400_2_p19, n7400_2_p11, d_2, c_2, b_2, a_2
  LED led_2 (.in(n7474_1_p5));

  // Notes on the sheet:
  //   3)
  //   !d
  //   1)
  //   4)
  //   2)
  //   a
  //   c
  //   b
  //   d
  //   !b
  //   1) a !b !d
  //   2) !(ac)
  //   3) !(1 && 2)
  //   4) !(bcd)
  //   1)
  //   2)
  //   c
  //   !d
  //   a
  //   b
  //   d
  //   !b
endmodule
